# Fritzing sketch Sucrose Pump (saved by Fritzing 0.9.3b)
perfboards: 1

parts:
  U1 = mystery part, 3 pins [chip_label=TIP120]
  L1 = Solenoid
  J1 = female pin header, 2 pins [form="♀ (female)"]
  D1 = Rectifier Diode [part_number=1N4001 package="300 mil [THT]"]
  부품1 = Arduino Uno (Rev3)
  R1 = Resistor [tolerance=±5% resistance=2.2k package=THT]
  Opto = IC, DIP package, 4 pins [chip_label=Opto]
  R2 = Resistor [tolerance=±5% resistance=300 package=THT]
  R5 = Resistor [tolerance=±5% resistance=100 package=THT]
  J3 = female pin header, 2 pins [form="♀ (female)"]
  J4 = female pin header, 2 pins [form="♀ (female)"]  # not connected
  J5 = female pin header, 3 pins [form="♀ (female)"]
  J6 = female pin header, 4 pins [form="♀ (female)"]
  J7 = female pin header, 3 pins [form="♀ (female)"]
  R6 = Resistor [tolerance=±5% resistance=10k package=THT]
  J9 = female pin header, 3 pins [form="♀ (female)"]
  R7 = Resistor [tolerance=±5% resistance=10k package=THT]
  J10 = female pin header, 2 pins [form="♀ (female)"]
  J11 = female pin header, 2 pins [form="♀ (female)"]
  J12 = female pin header, 4 pins [form="♀ (female)"]
  J13 = female pin header, 2 pins [form="♀ (female)"]
  J14 = female pin header, 2 pins [form="♀ (female)"]
  J15 = female pin header, 2 pins [form="♀ (female)"]
  J16 = female pin header, 3 pins [form="♀ (female)"]
  J17 = female pin header, 3 pins [form="♀ (female)"]
  J18 = female pin header, 2 pins [form="♀ (female)"]

nets:
  N1: U1.pin1, R1.Pin_1
  N2: U1.pin2, L1.pin1, J1.pin2, D1.anode
  N3: U1.pin3, 부품1.D7, R2.Pin_0, J5.pin3, J7.pin3, R6.Pin_1, J9.pin3, R7.Pin_1, J16.pin3, J17.pin3
  N4: L1.pin2, J1.pin1, D1.cathode, 부품1.VIN, J6.pin1
  N5: 부품1.D8, J12.pin1
  N6: 부품1.D9_PWM, R6.Pin_0, J11.pin1, J12.pin2
  N7: 부품1.D10_PWM/SS, J5.pin2, J12.pin3, J16.pin2
  N8: 부품1.D11_PWM/MOSI, J7.pin2, J12.pin4, J17.pin2
  N9: 부품1.D5_PWM, R1.Pin_0, J9.pin1
  N10: 부품1.D6_PWM, J9.pin2
  N11: 부품1.5V, J5.pin1, J7.pin1, J10.pin2, J11.pin2, J16.pin1, J17.pin1, J18.pin2
  N12: 부품1.GND, Opto.pin2, J6.pin2, J6.pin3
  N13: Opto.pin1, R2.Pin_1, R5.Pin_1
  N14: J3.pin1, J13.pin1
  N15: J3.pin2, J13.pin2
  N16: R7.Pin_0, J10.pin1, J18.pin1
  N17: J14.pin1, J15.pin1
  N18: J14.pin2, J15.pin2

notes:
  D8,9,10,11
  to TDT
  to Control (Lick)
  DIN
  DOUT
  Lick Sensor
  Manual Button
  Empty
  Lick Inhibit
  POW
  to Valve
  12V IN
  D5,6,7
  Schematic
  https://github.com/knowblesse/LobsterUnitCode/tree/master/Schematic
